# Fritzing sketch First Prototype (saved by Fritzing 0.9.6b)
breadboards: 1

parts:
  Mod1 = TTGO-T-Call-V1.3-ESP32 [package=THT]
  U1 = OBDII [package=obdii]
  IC1 = DIP - 6 pins [chip_label=SN65HVD230 package="DIP (Dual Inline) [THT]"]

nets:
  3V3: Mod1.3V3, IC1.3V3
  N1: Mod1.15, IC1.CRX
  N2: Mod1.18, IC1.CTX
  GND: Mod1.GND, IC1.GND
  N3: U1.CANHIGH, IC1.CANH
  N4: U1.CANLOW, IC1.CANL

custom parts:
  TTGO-T-Call-V1.3-ESP32: LILYGO® TTGO T-Call V1.3 ESP32 Wireless Module GPRS Antenna SIM Card SIM800L Module
  DIP - 6 pins: A DIP stand-in part for whatever IC you want. With 6 pins on a 300mil dual inline package (DIP) footprint.
