# Fritzing sketch Prototype (saved by Fritzing 0.9.6b)
breadboards: 1

parts:
  LILYGO®_TTGO_T-Call_V1_4 = TTGO-T-Call-V1.3-ESP32 [package=THT]
  SSD1306_Adafruit = WeMos D1 Mini OLED Shield
  RTC_-_DS3231 = ZS-042 RTC Module
  U1 = OBDII [package=obdii]
  SN65HVD230 = DIP - 6 pins [chip_label=SN65HVD230 package="DIP (Dual Inline) [THT]"]  # not connected

nets:
  3V3: LILYGO®_TTGO_T-Call_V1_4.NC, SSD1306_Adafruit.3V3, RTC_-_DS3231.VCC
  GND: LILYGO®_TTGO_T-Call_V1_4.GND, SSD1306_Adafruit.G, RTC_-_DS3231.GND
  N1: LILYGO®_TTGO_T-Call_V1_4.15, LILYGO®_TTGO_T-Call_V1_4.18
  N2: U1.9, U1.J1850BUS, U1.12, U1.13, U1.CANLOW, U1.ISOL-LINE, U1.BATTPOWER

custom parts:
  TTGO-T-Call-V1.3-ESP32: LILYGO® TTGO T-Call V1.3 ESP32 Wireless Module GPRS Antenna SIM Card SIM800L Module
  DIP - 6 pins: A DIP stand-in part for whatever IC you want. With 6 pins on a 300mil dual inline package (DIP) footprint.
